// Logisim project circuit.circ as structural Verilog: 5 circuits, main circuit Main
module Main (
);

  wire Clock, not_1_out, not_2_out, or_1_out, Reset, Run, Terminate, Terminated, Write_RAM, Write_Register;
  wire [1:0] Address_1, Address_2, multiplexer_1_out, multiplexer_2_out, Out_Address;
  wire [3:0] Operator;
  wire [4:0] Instruction_Address;
  wire [7:0] Accumulator, Instruction, New_Accumulator_Value, Out_Value, ram_1_data, RAM_Value, Rx, Ry;

  Clock clock_1 (.out(Clock));
  Button u_Reset (.out(Reset));
  Executor executor_1 (
    .Value_1(Rx), .Value_2(Ry), .Accumulator(Accumulator), .Address_2(Address_2),
    .Accumulator_2(New_Accumulator_Value), .Write_Register(Write_Register), .Terminate(Terminate),
    .Operator(Operator), .Address_1(Address_1), .Run(Run), .Address(Out_Address), .RAM_Value(RAM_Value),
    .Value(Out_Value), .Write_RAM(Write_RAM), .Clock(Clock));
  Instruction_Splitter instruction_splitter_1 (
    .Instruction(Instruction), .Address_2(Address_2), .Address_1(Address_1), .Operator(Operator));
  Program_Counter program_counter_1 (
    .Clock(Clock), .Finish(Terminate), .Reset(Reset), .Instruction(Instruction_Address),
    .Finished(Terminated), .Running(Run));
  Multiplexer #(.width(2)) multiplexer_1 (
    .in0(Address_1), .in1(Out_Address), .out(multiplexer_1_out), .sel(Write_Register));  // open: en
  Registers registers_1 (
    .Address_1(multiplexer_1_out), .Address_2(Address_2), .Value_1(Out_Value), .Write(Write_Register),
    .Value_1_2(Rx), .Value_2(Ry), .Clear(or_1_out));
  or or_1 (or_1_out, Terminated, Reset);
  Multiplexer #(.width(2)) multiplexer_2 (
    .in0(Address_2), .in1(Out_Address), .out(multiplexer_2_out), .sel(Write_RAM));  // open: en
  not not_1 (not_1_out, Write_RAM);
  ROM #(.addrWidth(5)) rom_1 (.addr(Instruction_Address), .data(Instruction));  // open: sel
  RAM #(.addrWidth(2), .bus("asynch")) ram_1 (
    .addr(multiplexer_2_out), .data(ram_1_data), .ld(not_1_out));  // open: sel, clr
  assign ram_1_data = not_2_out ? Out_Value : 8'bz;  // Controlled_Buffer controlled_buffer_1
  not not_2 (not_2_out, not_1_out);
  Register #(.trigger("high")) register_1 (
    .D(New_Accumulator_Value), .Q(Accumulator), .clk(Clock), .clr(or_1_out));  // open: en
  Multiplexer #(.width(8)) multiplexer_3 (
    .in0(RAM_Value), .in1(ram_1_data), .out(RAM_Value), .sel(not_1_out));  // open: en

  // Notes on the sheet:
  //   Clock do Computador
  //   Unidade de Controle
  //   Contador de Programa
  //   Registradores
  //   Memória de Programa (ROM)
  //   Memória de Dados (RAM)
  //   contents of rom_1 (hex, n*v repeats v):
  //   d0 d5 da 86 cc 93 cc ef a0
  //   Acumulador
endmodule

module Executor (
  input  Run,
  input  Clock,
  input  [1:0] Address_1,
  input  [1:0] Address_2,
  input  [7:0] Value_1,
  input  [7:0] Value_2,
  input  [7:0] RAM_Value,
  input  [3:0] Operator,
  input  [7:0] Accumulator,
  output [7:0] Accumulator_2,
  output Terminate,
  output [1:0] Address,
  output [7:0] Value,
  output Write_Register,
  output Write_RAM
);

  wire and_2_out, and_3_out, and_11_out, comparator_1_eq, comparator_2_eq, comparator_3_eq, comparator_4_eq,
       comparator_5_eq, comparator_6_eq, comparator_7_eq, MOV_1, MOV_2, or_1_out, or_2_out, RDM, Run_t, STR;
  wire [7:0] adder_1_out, multiplier_1_out;

  Comparator #(.width(4)) comparator_1 (.a(Operator), .b(4'b1000), .eq(comparator_1_eq));  // open: gt, lt
  Comparator #(.width(4)) comparator_2 (.a(Operator), .b(4'b1001), .eq(comparator_2_eq));  // open: gt, lt
  Comparator #(.width(4)) comparator_3 (.a(Operator), .b(4'b1010), .eq(comparator_3_eq));  // open: gt, lt
  Comparator #(.width(4)) comparator_4 (.a(Operator), .b(4'b1011), .eq(comparator_4_eq));  // open: gt, lt
  Comparator #(.width(4)) comparator_5 (.a(Operator), .b(4'b1100), .eq(comparator_5_eq));  // open: gt, lt
  Comparator #(.width(4)) comparator_6 (.a(Operator), .b(4'b1101), .eq(comparator_6_eq));  // open: gt, lt
  Comparator #(.width(4)) comparator_7 (.a(Operator), .b(4'b1110), .eq(comparator_7_eq));  // open: gt, lt
  and and_1 (Run_t, Run, Clock);
  and and_2 (and_2_out, Run_t, comparator_1_eq);
  and and_3 (and_3_out, Run_t, comparator_2_eq);
  and and_4 (Terminate, Run_t, comparator_3_eq);
  and and_5 (MOV_1, Run_t, comparator_4_eq);
  and and_6 (MOV_2, Run_t, comparator_5_eq);
  and and_7 (RDM, Run_t, comparator_6_eq);
  and and_8 (STR, Run_t, comparator_7_eq);
  Multiplier multiplier_1 (.a(Value_1), .b(Value_2), .out(multiplier_1_out));  // open: cin, cout
  assign Accumulator_2 = and_2_out ? multiplier_1_out : 8'bz;  // Controlled_Buffer controlled_buffer_1
  or or_1 (or_1_out, MOV_1, RDM, MOV_2);
  and and_9 (Write_Register, or_1_out, Run_t);
  and and_10 (Write_RAM, Run_t, STR);
  Adder adder_1 (.a(Value_1), .b(Value_2), .out(adder_1_out));  // open: cin, cout
  assign Accumulator_2 = and_3_out ? adder_1_out : 8'bz;  // Controlled_Buffer controlled_buffer_2
  and and_11 (and_11_out, ~and_2_out, ~and_3_out);  // AND_Gate
  assign Accumulator_2 = and_11_out ? Accumulator : 8'bz;  // Controlled_Buffer controlled_buffer_3
  assign Value = or_2_out ? Value_2 : 8'bz;  // Controlled_Buffer controlled_buffer_4
  or or_2 (or_2_out, MOV_1, STR);
  assign Value = MOV_2 ? Accumulator : 8'bz;  // Controlled_Buffer controlled_buffer_5
  assign Value = RDM ? RAM_Value : 8'bz;  // Controlled_Buffer controlled_buffer_6

  assign Address = Address_1;

  // Notes on the sheet:
  //   MUL
  //   ADD
  //   HLT
  //   MOV
  //   MOV
  //   RDM
  //   STR
endmodule

// Splitter
module Instruction_Splitter (
  input  [7:0] Instruction,
  output [1:0] Address_2,
  output [1:0] Address_1,
  output [3:0] Operator
);


  assign Address_1 = Instruction[3:2];
  assign Address_2 = Instruction[1:0];
  assign Operator = Instruction[7:4];
endmodule

module Registers (
  input  [1:0] Address_1,
  input  [1:0] Address_2,
  input  [7:0] Value_1,
  input  Write,
  input  Clear,
  output [7:0] Value_1_2,
  output [7:0] Value_2
);

  wire and_1_out, demultiplexer_1_out0, demultiplexer_1_out1, demultiplexer_1_out2, demultiplexer_1_out3;
  wire [7:0] R0, R1, R2, R3;

  and and_1 (and_1_out, 1'b1, Write);
  Demultiplexer #(.select(2)) demultiplexer_1 (
    .out0(demultiplexer_1_out0), .out1(demultiplexer_1_out1), .out2(demultiplexer_1_out2),
    .out3(demultiplexer_1_out3), .in(and_1_out), .sel(Address_1));  // open: en
  Register register_1 (.D(Value_1), .Q(R3), .clk(demultiplexer_1_out0), .clr(Clear));  // open: en
  Register register_2 (.D(Value_1), .Q(R2), .clk(demultiplexer_1_out1), .clr(Clear));  // open: en
  Register register_3 (.D(Value_1), .Q(R1), .clk(demultiplexer_1_out2), .clr(Clear));  // open: en
  Register register_4 (.D(Value_1), .Q(R0), .clk(demultiplexer_1_out3), .clr(Clear));  // open: en
  Multiplexer #(.select(2), .width(8)) multiplexer_1 (
    .in0(R3), .in1(R2), .in2(R1), .in3(R0), .out(Value_1_2), .sel(Address_1));  // open: en
  Multiplexer #(.select(2), .width(8)) multiplexer_2 (
    .in0(R3), .in1(R2), .in2(R1), .in3(R0), .out(Value_2), .sel(Address_2));  // open: en

  // Other names for the same wires on the sheet: Value[7:0] = Value_1
endmodule

// Counter
module Program_Counter (
  input  Clock,
  input  Finish,
  input  Reset,
  output [4:0] Instruction,
  output Finished,
  output Running
);

  wire and_1_out, counter_1_carry, or_1_out;

  Counter #(.width(5), .max('h1f), .trigger("falling")) counter_1 (
    .Q(Instruction), .carry(counter_1_carry), .clk(and_1_out), .clr(Reset));  // open: load, D, count
  and and_1 (and_1_out, Clock, Running);
  or or_1 (or_1_out, counter_1_carry, Finish);
  Counter #(.width(1), .max('h1), .trigger("falling")) counter_2 (
    .Q(Finished), .clk(or_1_out), .clr(Reset));  // open: load, D, count, carry
  not not_1 (Running, Finished);

  // Other names for the same wires on the sheet: Run = Running
endmodule
